# Fritzing sketch Briefkastenschild (saved by Fritzing 0.9.3b)
breadboards: 1

parts:
  LCD1 = LCD screen
  Bauteil1 = Arduino Uno (Rev3)
  R1 = Resistor [tolerance=±5% resistance=4.7k package=THT]
  R2 = Resistor [tolerance=±5% resistance=150 package=THT]
  D2F1 = D2F-FL Omron Snap Action Limit Switch with Level

nets:
  VSS: LCD1.VSS, LCD1.R/W, Bauteil1.GND, D2F1.COM
  VDD: LCD1.VDD, Bauteil1.5V
  N1: LCD1.V0, LCD1.LED+, R1.Pin_0, R2.Pin_1
  N2: LCD1.RS, Bauteil1.D8
  N3: LCD1.E, Bauteil1.D9_PWM
  N4: LCD1.DB4, Bauteil1.D4
  N5: LCD1.DB5, Bauteil1.D5_PWM
  N6: LCD1.DB6, Bauteil1.D6_PWM
  N7: LCD1.DB7, Bauteil1.D7
  N8: Bauteil1.D10_PWM/SS, D2F1.NO

custom parts:
  D2F-FL Omron Snap Action Limit Switch with Level: Snap action switch with stainless steel lever.
